# Fritzing sketch forja-dracula (saved by Fritzing 0.9.8b)
breadboards: 1

parts:
  Mega = Arduino Mega 2560 (Rev3)
  SENSOR_RGB_CARRIL_1 = Adafruit TCS34725 RGB Color Sensor [part_number="Adafruit #1334"]
  SENSOR_RGB_CARRIL_2 = Adafruit TCS34725 RGB Color Sensor [part_number="Adafruit #1334"]
  SENSOR_RGB_CARRIL_3 = Adafruit TCS34725 RGB Color Sensor [part_number="Adafruit #1334"]
  SENSOR_RGB_CARRIL_4 = Adafruit TCS34725 RGB Color Sensor [part_number="Adafruit #1334"]

nets:
  GND: Mega.GND, SENSOR_RGB_CARRIL_1.GND, SENSOR_RGB_CARRIL_2.GND, SENSOR_RGB_CARRIL_3.GND, SENSOR_RGB_CARRIL_4.GND
  D22: Mega.D22, SENSOR_RGB_CARRIL_1.SDA
  D23: Mega.D23, SENSOR_RGB_CARRIL_1.SCL
  D24: Mega.D24, SENSOR_RGB_CARRIL_2.SDA
  D25: Mega.D25, SENSOR_RGB_CARRIL_2.SCL
  D26: Mega.D26, SENSOR_RGB_CARRIL_3.SDA
  D27: Mega.D27, SENSOR_RGB_CARRIL_3.SCL
  D28: Mega.D28, SENSOR_RGB_CARRIL_4.SDA
  D29: Mega.D29, SENSOR_RGB_CARRIL_4.SCL
  5V: SENSOR_RGB_CARRIL_1.VIN, SENSOR_RGB_CARRIL_2.VIN, SENSOR_RGB_CARRIL_3.VIN, SENSOR_RGB_CARRIL_4.VIN

custom parts:
  Adafruit TCS34725 RGB Color Sensor: Your electronics can now see in dazzling color with this lovely color light sensor. We found the best color sensor on the market, the TCS34725, which has RGB and Clear light sensing elements. An IR blocking filter, integrated on-chip and localized to the color sensing photodiodes, minimizes the IR spectral component of the incoming light and allows color measurements to be made accurately. The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
